# Fritzing sketch circuit_diagram (saved by Fritzing 0.9.3b)
perfboards: 1

parts:
  U1 = LM 358 Dual Op-Amp [package="DIP8 [THT]"]
  パーツ1 = Arduino Nano (Rev3.0)
  IC1 = IC, DIP package, 8 pins [chip_label=LT1167]
  J1 = female pin header, 3 pins [form="♀ (female)"]
  J2 = female pin header, 4 pins [form="♀ (female)"]
  R1 = Resistor [tolerance=±5% resistance=100 package=THT]
  R3 = Resistor [tolerance=±5% resistance=2k package=THT]
  R2 = Resistor [tolerance=±5% resistance=4.7k package=THT]
  C1 = Ceramic Capacitor [capacitance=100nF package="100 mil [THT, multilayer]"]
  C2 = Ceramic Capacitor [capacitance=100nF package="100 mil [THT, multilayer]"]

nets:
  N1: U1.connector0, U1.connector1, IC1.pin5, J1.pin1, C1.0, C2.1
  N2: U1.connector2, R3.Pin_0, R2.Pin_1
  GND: U1.connector3, パーツ1.GND, IC1.pin4, J2.pin2, R3.Pin_1, C2.0
  5V: U1.connector7, パーツ1.5V, IC1.pin7, R2.Pin_0, C1.1
  N3: パーツ1.D1/TX, J2.pin4
  N4: パーツ1.D0/RX, J2.pin3
  N5: パーツ1.A0, IC1.pin6
  N6: パーツ1.3V3, J2.pin1
  N7: IC1.pin1, R1.Pin_0
  N8: IC1.pin2, J1.pin2
  N9: IC1.pin3, J1.pin3
  N10: IC1.pin8, R1.Pin_1

notes:
  BT
  pin1:VCC
  pin2:GND
  pin3:TXD
  pin4:RXD
  体重計
  pin1:GNN
